// Digital circuit ALU.dig as structural Verilog
module ALU (
  input  [63:0] A,
  input  [63:0] B,
  input  [3:0] OP,
  output [63:0] X,
  output [4:0] F
);

  wire add_1_c_o, overflow, sub_1_c_o;
  wire [63:0] add_1_s, div_1_q, mul_1_mul, sub_1_s;

  Add #(.Bits(64)) add_1 (.a(A), .b(B), .c_i(1'b0), .s(add_1_s), .c_o(add_1_c_o));
  Sub #(.Bits(64)) sub_1 (.a(A), .b(B), .c_i(1'b0), .s(sub_1_s), .c_o(sub_1_c_o));
  Mul #(.Signed("true"), .Bits(32)) mul_1 (.a(A[31:0]), .b(B[31:0]), .mul(mul_1_mul));
  Div #(.Bits(64)) div_1 (.a(A), .b(B), .q(div_1_q));  // open: r
  Comparator #(.Bits(64)) comparator_1 (.a(A), .b(B), .gt(F[0]), .eq(F[1]), .lt(F[2]));
  Multiplexer #(.Selector_Bits(4)) multiplexer_1 (
    .sel(OP), .in_0(add_1_c_o), .in_1(sub_1_c_o), .in_2(1'b0), .in_3(1'b0), .in_4(1'b0), .in_5(1'b0),
    .in_6(1'b0), .in_7(1'b0), .in_8(1'b0), .in_9(1'b0), .in_10(1'b0), .in_11(1'b0), .in_12(1'b0),
    .in_13(1'b0), .in_14(1'b0), .in_15(1'b0), .out(overflow));
  Multiplexer #(.Selector_Bits(4), .Bits(64)) multiplexer_2 (
    .sel(OP), .in_0(add_1_s), .in_1(sub_1_s), .in_2(mul_1_mul), .in_3(div_1_q), .in_4({64{1'b0}}),
    .in_5({64{1'b0}}), .in_6({64{1'b0}}), .in_7({64{1'b0}}), .in_8({64{1'b0}}), .in_9({64{1'b0}}),
    .in_10({64{1'b0}}), .in_11({64{1'b0}}), .in_12({64{1'b0}}), .in_13({64{1'b0}}), .in_14({64{1'b0}}),
    .in_15({64{1'b0}}), .out(X));
  Comparator #(.Signed("true"), .Bits(64)) comparator_2 (.a(X), .b({64{1'b0}}), .eq(F[3]), .lt(F[4]));  // open: gt

  // Notes on the sheet:
  //   A: Number A
  //   B: Number B
  //   X: Output X
  //   OP: Operation to perform between A and B
  //   F: Flag Outputs, 5 bit output.
  //   0 - Greater Than
  //   1 - Equal to
  //   2 - Lesser Than
  //   3 - Z, high if output == zero
  //   4 - N, high if output is negative
  //   Add
  //   Subtract
  //   Multiply
  //   Divide
endmodule
