// Digital circuit CPU.dig as structural Verilog
module CPU (
  input  [63:0] Databus_Manual_Input,
  input  CPU_Clock
);

  wire ADDRw, CCclr, clock, comparator_1_gt, comparator_2_gt, D1out, Databus_Manual_Switch_out, DBout,
       driverinvsel_3_out, ETf, GTf, HLT, IRw, LTf, Manual_Clock_Stepper_out, Manual_Stepping_out,
       multiplexer_1_out, Nf, not_1_out, or_1_out, PAinc, PAw, RAMr, RAMw, RAr, RAw, RBr, RBw, ROMr, SRr,
       SRw, Zf;
  wire [2:0] CPAw;
  wire [3:0] ALUop, Control_Counter_out;
  wire [4:0] alu_1_f;
  wire [6:0] Instruction_Register_q;
  wire [23:0] add_1_s, Address_Register_q, driverinvsel_2_out, Program_Address_Register_q;
  wire [24:4] Logic_Table_d;
  wire [43:29] undriven, undriven_2;
  wire [56:0] Instruction_Register_q_2;
  wire [63:0] alu_1_x, bitextender_1_out, bitextender_2_out, bitextender_3_out, databus, RA, Register_B_q,
       Sum_Register_q;

  Register #(.Bits(64)) Register_A (.D(databus), .C(clock), .en(RAw), .Q(RA));
  Register #(.Bits(64)) Register_B (.D(databus), .C(clock), .en(RBw), .Q(Register_B_q));
  or or_1 (or_1_out, HLT, Manual_Stepping_out);
  DipSwitch #(.dipDefault("true")) Manual_Stepping (.out(Manual_Stepping_out));
  assign databus = Databus_Manual_Switch_out ? Databus_Manual_Input : 64'bz;  // Driver driver_1
  DipSwitch Databus_Manual_Switch (.out(Databus_Manual_Switch_out));
  Button Manual_Clock_Stepper (.out(Manual_Clock_Stepper_out));
  assign clock = or_1_out ? Manual_Clock_Stepper_out : 1'bz;  // Driver driver_2
  assign clock = ~or_1_out ? CPU_Clock : 1'bz;  // DriverInvSel driverinvsel_1
  assign databus = RAr ? RA : 64'bz;  // Driver driver_3
  assign databus = RBr ? Register_B_q : 64'bz;  // Driver driver_4
  ALU alu_1 (.A(RA), .B(databus), .OP(ALUop), .X(alu_1_x), .F(alu_1_f));
  Register #(.Bits(24)) Address_Register (.D(databus[23:0]), .C(clock), .en(ADDRw), .Q(Address_Register_q));
  Register #(.Bits(64)) Sum_Register (.D(alu_1_x), .C(clock), .en(SRw), .Q(Sum_Register_q));
  Register #(.Bits(5)) Flag_Register (.D(alu_1_f), .C(clock), .en(SRw), .Q({Nf, Zf, LTf, ETf, GTf}));
  Comparator #(.Bits(3)) comparator_1 (.a(CPAw), .b(3'b000), .gt(comparator_1_gt));  // open: eq, lt
  assign databus = SRr ? Sum_Register_q : 64'bz;  // Driver driver_5
  RAMDualPort #(.AddrBits(24), .Bits(64)) ramdualport_1 (
    .A(Address_Register_q), .Din(databus), .str(RAMw), .C(clock), .ld(RAMr), .D(databus));
  Multiplexer #(.Selector_Bits(3)) multiplexer_1 (
    .sel(CPAw), .in_0(1'b0), .in_1(GTf), .in_2(ETf), .in_3(LTf), .in_4(Zf), .in_5(Nf), .in_6(1'b0),
    .in_7(1'b0), .out(multiplexer_1_out));
  assign PAw = comparator_1_gt ? multiplexer_1_out : 1'bz;  // Driver driver_6
  Counter #(.Bits(4)) Control_Counter (.en(1'b1), .C(not_1_out), .clr(CCclr), .out(Control_Counter_out));  // open: ovf
  not not_1 (not_1_out, clock);
  Register #(.Bits(64)) Instruction_Register (
    .D(databus), .C(clock), .en(IRw), .Q({Instruction_Register_q_2, Instruction_Register_q}));
  assign driverinvsel_2_out = ~PAinc ? databus[23:0] : 24'bz;  // DriverInvSel driverinvsel_2
  assign driverinvsel_3_out = ~PAinc ? PAw : 1'bz;  // DriverInvSel driverinvsel_3
  assign driverinvsel_3_out = PAinc ? 1'b1 : 1'bz;  // Driver driver_7
  BitExtender #(.inputBits(44), .outputBits(64)) bitextender_1 (
    .in(Instruction_Register_q_2[43:0]), .out(bitextender_1_out));
  BitExtender #(.inputBits(44), .outputBits(64)) bitextender_2 (
    .in({undriven, Instruction_Register_q_2[28:0]}), .out(bitextender_2_out));
  BitExtender #(.inputBits(44), .outputBits(64)) bitextender_3 (
    .in({undriven_2, Instruction_Register_q_2[56:28]}), .out(bitextender_3_out));
  assign driverinvsel_2_out = PAinc ? add_1_s : 24'bz;  // Driver driver_8
  Register #(.Bits(24)) Program_Address_Register (
    .D(driverinvsel_2_out), .C(clock), .en(driverinvsel_3_out), .Q(Program_Address_Register_q));
  Add #(.Bits(24)) add_1 (.a(Program_Address_Register_q), .b({24{1'b0}}), .c_i(1'b1), .s(add_1_s));  // open: c_o
  EEPROM #(.AddrBits(12), .Bits(25)) Logic_Table (
    .A({Instruction_Register_q_2[0], Instruction_Register_q, Control_Counter_out}), .CS(1'b1), .WE(1'b0),
    .OE(1'b1),
    .D({Logic_Table_d[24:23], HLT, CPAw, ALUop, DBout, RAw, RAr, RBw, RBr, SRw, SRr, ADDRw, RAMw, RAMr, Logic_Table_d[4], CCclr, PAinc, ROMr, IRw}));
  assign databus = DBout ? bitextender_1_out : 64'bz;  // Driver driver_9
  assign databus = D1out ? bitextender_2_out : 64'bz;  // Driver driver_10
  assign databus = D1out ? bitextender_3_out : 64'bz;  // Driver driver_11
  EEPROM #(.AddrBits(24), .isProgramMemory("true"), .Bits(64)) eeprom_1 (
    .A(Program_Address_Register_q), .CS(1'b1), .WE(1'b0), .OE(ROMr), .D(databus));
  assign PAw = ~comparator_2_gt ? Logic_Table_d[4] : 1'bz;  // DriverInvSel driverinvsel_4
  Comparator #(.Bits(3)) comparator_2 (.a(CPAw), .b(3'b000), .gt(comparator_2_gt));  // open: eq, lt
  // Pins of 23 and 25 bits meet at {Logic_Table_d[24:23], HLT, CPAw, ALUop, DBout, RAw, RAr, RBw, RBr, SRw, SRr, ADDRw, RAMw, RAMr, Logic_Table_d[4], CCclr, PAinc, ROMr, IRw}
  // Pins of 44 and 57 bits meet at Instruction_Register_q_2
  // Pins of 29 and 44 bits meet at {undriven, Instruction_Register_q_2[28:0]}
  // Pins of 29 and 44 bits meet at {undriven_2, Instruction_Register_q_2[56:28]}

  // Notes on the sheet:
  //   CPU_Clock: Hz: 20
  //   Clock Control
  //   Manual Databus Control
  //   Register A
  //   Register B
  //   ALU & Sum Register
  //   RAM & Address Register
  //   Conditional Jump
  //   Control Logic
  //   ROM & Program Address Register
  //   contents of Logic_Table (hex, n*v repeats v):
  //   7,8,14*0,7,200e,14*0,7,4080,1048,13*0,7,4080,2028,13*0,7,80e,14*0
  //   ,7,4080,448,13*0,7,4080,828,13*0,7,4080,4e,13*0,7,4080,220,2108
  //   ,12*0,7,4080,8220,2108,12*0,7,4080,10220,2108,12*0,7,4080,18220
  //   ,2108,12*0,7,4018,14*0,7,204008,14*0,7,284008,14*0,7,1000080,220
  //   ,880008,12*0,7,1000080,220,900008,12*0,7,1000080,220,980008,12*0
  //   ,7,400000
  //   contents of eeprom_1 (hex, n*v repeats v):
  //   7,1,100007,a,8,400011,1
endmodule
