// Digital circuit GPU.dig as structural Verilog
module GPU (
  input  [10:0] _0,
  input  _1,
  input  _2,
  input  _3,
  input  _4,
  input  [6:0] _5,
  output [6:0] out_2
);

  wire [6:0] graphiccard_1_d;

  GraphicCard #(.graphicHeight(20), .Bits(7), .graphicWidth(32)) graphiccard_1 (
    .A(_0), .str(_1), .C(_2), .ld(_3), .B(_4), .D(graphiccard_1_d));
  assign out_2 = _3 ? graphiccard_1_d : 7'bz;  // Driver driver_1
  assign graphiccard_1_d = ~_3 ? _5 : 7'bz;  // DriverInvSel driverinvsel_1

  // Other names for the same wires on the sheet: read = _3
endmodule
